# Fritzing sketch domination (saved by Fritzing 0.9.3b)
breadboards: 1

parts:
  Part1 = Arduino Uno (Rev3)
  LED1 = LED - 5mm [color="Red (633nm)" package="5 mm [THT]"]
  LED2 = LED - 5mm [color="Blue (470nm)" package="5 mm [THT]"]  # not connected
  S1 = Round Pushbutton
  S2 = Round Pushbutton  # not connected
  R1 = Resistor [tolerance=±5% resistance=220 package="0805 [SMD]"]  # not connected

nets:
  N1: Part1.D8, S1.leg0
  N2: Part1.D9_PWM, LED1.cathode
  N3: Part1.GND, LED1.anode, S1.leg1
